# Fritzing sketch IR Sensor fritzing Sketch (saved by Fritzing 0.9.3b)
breadboards: 1

parts:
  Part1 = Arduino Uno (Rev3)
  M1 = fc-51 [package=THT]
  M2 = fc-51 [package=THT]
  Part2 = LCD1602-I2C

nets:
  N1: Part1.A4/SDA, Part2.SDA
  N2: Part1.A5/SCL, Part2.SCL
  N3: Part1.D5_PWM, M1.pin1
  N4: Part1.D7, M2.pin1
  5V: Part1.5V, M1.pin3, M2.pin3, Part2.VCC
  GND: Part1.GND, M1.pin2, M2.pin2, Part2.GND

custom parts:
  LCD1602-I2C: A standard character display, usually with 2x16 characters. Comes in many colors with LCM1602 IIC attached.
